# Fritzing sketch resin_light_diagram (saved by Fritzing 0.9.4)
circuit board: 10cm x 6cm
breadboards: 1

parts:
  Attiny85_board = Digispark
  LED1_Flickering_5v = LED - 5mm [color="Red (633nm)" package="5 mm [THT]"]
  LED2_Flickering_5v = LED - 5mm [color="Red (633nm)" package="5 mm [THT]"]
  LED3_Flickering_5v = LED - 5mm [color="Red (633nm)" package="5 mm [THT]"]
  S1 = Round Pushbutton
  LED4_Flickering_5v = LED - 5mm [color="Red (633nm)" package="5 mm [THT]"]
  BAT1 = BC9VPC [package=bc9vpc]
  R1 = Resistor [tolerance=±5% resistance=10k package="1206 [SMD]"]
  Power_Switch = SPST Switch [package=switch-spdt_lock.007s]

nets:
  N1: Attiny85_board.VCC, S1.leg1
  N2: Attiny85_board.GND, LED1_Flickering_5v.cathode, LED2_Flickering_5v.cathode, LED3_Flickering_5v.cathode, LED4_Flickering_5v.cathode, BAT1.V-, R1.Pin_0
  N3: Attiny85_board.VIN, Power_Switch.P
  N4: Attiny85_board.P0, LED4_Flickering_5v.anode
  N5: Attiny85_board.P1, LED3_Flickering_5v.anode
  N6: Attiny85_board.P2, S1.leg0, R1.Pin_1
  N7: Attiny85_board.P3, LED2_Flickering_5v.anode
  N8: Attiny85_board.P4, LED1_Flickering_5v.anode
  N9: BAT1.V+, Power_Switch.S

custom parts:
  Digispark: The Digispark is an Attiny85 based microcontroller development board similar to the Arduino line, only cheaper, smaller, and a bit less powerful. With a whole host of shields to extend its functionality and the ability to use the familiar Arduino IDE the Digispark is a great way to jump into electronics, or perfect for when an Arduino is too big or too much.
