# Fritzing sketch mcontact-less-servo-leds (saved by Fritzing 0.9.6b)
breadboards: 1

parts:
  Part1 = Arduino Nano (Rev3.0)
  Part2 = Adafruit APDS-9960 [part_number="Adafruit #3595"]
  J1 = Basic Servo
  LED1 = DUO LED RG [package="5 mm [THT]"]

nets:
  GND: Part1.GND, Part2.GND, J1.gnd, LED1.green_anode
  N1: Part1.D2, Part2.INT
  N2: Part1.D4, Part2.VIN
  N3: Part1.D5, LED1.common_cathode
  N4: Part1.D9, J1.pulse
  5V: Part1.5V, J1.vcc, LED1.red_anode
  N5: Part1.A5, Part2.SDA
  N6: Part1.A4, Part2.SCL
  3V3: Part1.3V3, Part2.3.3V

notes:
  pin d4 up.... to provide extra power
  5V

custom parts:
  Adafruit APDS-9960: The APDS9960 from Avago Technologies has an integrated IR LED and driver, along with four directional photodiodes that sense reflected IR energy from the LED. It's proximity detection feature allows it to measure the distance an object is from the front of the sensor (up to a few centimeters) with 8 bit resolution. Since there are four IR sensors, you can measure the changes in light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
