# Fritzing sketch mcontact-less (saved by Fritzing 0.9.4)
breadboards: 1

parts:
  KY-1 = Keyes Relay [package=THT]
  Part1 = Arduino Nano (Rev3.0)
  Part2 = Adafruit APDS-9960 [part_number="Adafruit #3595"]
  S1 = Toggle Switch [package=THT]
  VCC1 = 4 x AAA Battery Mount

nets:
  N1: KY-1.signal, Part1.D3
  N2: KY-1.power, Part1.5V
  GND: KY-1.ground, Part1.GND, Part2.GND, VCC1.-
  N3: Part1.D2, Part2.INT
  N4: Part1.VIN, S1.L2
  N5: Part1.A5, Part2.SDA
  N6: Part1.A4, Part2.SCL
  3V3: Part1.3V3, Part2.VIN, Part2.3.3V
  N7: S1.COM, VCC1.+

notes:
  3V
  5V

custom parts:
  Keyes Relay: The Keyes 5V relay module is suitable for SCM development, home appliance control. It uses a 5V~12V TIL control signal which can control DC / AC signal.
  Adafruit APDS-9960: The APDS9960 from Avago Technologies has an integrated IR LED and driver, along with four directional photodiodes that sense reflected IR energy from the LED. It's proximity detection feature allows it to measure the distance an object is from the front of the sensor (up to a few centimeters) with 8 bit resolution. Since there are four IR sensors, you can measure the changes in light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
