# Fritzing sketch annoier (saved by Fritzing 0.9.4)
breadboards: 1

parts:
  IC1 = Voltage Regulator [package=78xxl]
  C1 = Electrolytic Capacitor [capacitance=10µF package="100 mil [THT, electrolytic]"]
  C2 = Electrolytic Capacitor [capacitance=10µF package="100 mil [THT, electrolytic]"]
  12v = Power plug
  R1 = Photocell (LDR) [package=THT]
  Attiny85_board1 = Digispark
  R2 = Resistor [tolerance=±5% resistance=6.8k package="0402 [SMD]"]
  Q1 = Basic FET N-Channel [part_number=TIP120 package="TO220 [THT]"]
  L1 = Solenoid
  D1 = Rectifier Diode [part_number=1N4001 package="300 mil [THT]"]
  R3 = Resistor [tolerance=±5% resistance=1.5k package="2512 [SMD]"]

nets:
  GND: IC1.GND, C1.-, C2.-, 12v.GND, R1.pin_1, Q1.source
  N1: IC1.IN, C1.+, 12v.VCC, L1.pin2, D1.cathode
  N2: IC1.OUT, C2.+, R2.Pin_1
  N3: R1.pin_0, Attiny85_board1.P4, R2.Pin_0
  N4: Attiny85_board1.P0, R3.Pin_0
  N5: Q1.gate, R3.Pin_1
  N6: Q1.drain, L1.pin1, D1.anode

custom parts:
  Digispark: The Digispark is an Attiny85 based microcontroller development board similar to the Arduino line, only cheaper, smaller, and a bit less powerful. With a whole host of shields to extend its functionality and the ability to use the familiar Arduino IDE the Digispark is a great way to jump into electronics, or perfect for when an Arduino is too big or too much.
