# Fritzing sketch annoier2 (saved by Fritzing 0.9.4)
circuit board: 10cm x 6cm
breadboards: 1

parts:
  12v = Power plug
  R1 = Photocell (LDR) [package=THT]
  R2 = Resistor [tolerance=±5% resistance=6.8k package="0402 [SMD]"]
  Q1 = Basic FET N-Channel [part_number=TIP120 package="TO220 [THT]"]
  L1 = Solenoid
  D1 = Rectifier Diode [part_number=1N4001 package="300 mil [THT]"]
  R3 = Resistor [tolerance=±5% resistance=1.5k package="2512 [SMD]"]
  Part1 = Arduino Nano (Rev3.0)

nets (from the schematic view):
  GND: 12v.GND, R1.pin_1, Q1.source, Part1.GND
  VCC: 12v.VCC, L1.pin2, D1.cathode, Part1.VIN
  N1: R1.pin_0, R2.Pin_0, Part1.A0
  N2: R2.Pin_1, Part1.3V3
  N3: Q1.gate, R3.Pin_1
  N4: Q1.drain, L1.pin1, D1.anode
  N5: R3.Pin_0, Part1.D6
