# Fritzing sketch temporizzatore (saved by Fritzing 0.9.4)
circuit board: 10cm x 6cm
breadboards: 1

parts:
  Attiny85_board = Digispark
  S1 = Round Pushbutton
  LED4_Flickering_5v = LED - 5mm [color="Red (633nm)" package="5 mm [THT]"]
  R1 = Resistor [tolerance=±5% resistance=4.7k package="1206 [SMD]"]
  Power_Switch = SPST Switch [package=switch-spdt_lock.007s]
  VCC1 = 4 x AAA Battery Mount
  S2 = Round Pushbutton
  R2 = Resistor [tolerance=±5% resistance=4.7k package="1206 [SMD]"]
  J1 = Piezo Speaker
  Q1 = TRANSISTOR_NPN [package=to-92-ammo]
  R3 = Resistor [tolerance=±5% resistance=1k package="2010 [SMD]"]

nets:
  N1: Attiny85_board.VCC, S1.leg1, Power_Switch.P, S2.leg1, J1.pin2
  N2: Attiny85_board.GND, LED4_Flickering_5v.cathode, R1.Pin_0, VCC1.-, R2.Pin_0, Q1.C
  N3: Attiny85_board.P0, LED4_Flickering_5v.anode
  N4: Attiny85_board.P1, R3.Pin_0
  N5: Attiny85_board.P2, S1.leg0, R1.Pin_1
  N6: Attiny85_board.P3, S2.leg0, R2.Pin_1
  N7: Power_Switch.S, VCC1.+
  N8: J1.pin1, Q1.E
  N9: Q1.B, R3.Pin_1

custom parts:
  Digispark: The Digispark is an Attiny85 based microcontroller development board similar to the Arduino line, only cheaper, smaller, and a bit less powerful. With a whole host of shields to extend its functionality and the ability to use the familiar Arduino IDE the Digispark is a great way to jump into electronics, or perfect for when an Arduino is too big or too much.
