# Fritzing sketch trap-cam (saved by Fritzing 0.9.4)
circuit board: 8.46667cm x 5.64444cm
breadboards: 1

parts:
  Part1 = HC-SR501 Body Sensor Module
  R1 = Resistor [tolerance=±5% resistance=1k package="2010 [SMD]"]
  ESP32_-_Back1 = ESP32 - CAM
  R2 = Resistor [tolerance=±5% resistance=10k package="2010 [SMD]"]
  Q1 = NPN-Transistor [package="SOT-23 [SMD]"]
  U1 = LIPO-2000mAh [package=lipo-2000]

nets (from the schematic view):
  N1: Part1.VCC, Q1.2, U1.-
  N2: Part1.OUT, R1.Pin_1
  N3: Part1.GND, U1.+
  N4: R1.Pin_0, Q1.0
  N5: ESP32_-_Back1.GPIO13, R2.Pin_1
  N6: R2.Pin_0, Q1.1

custom parts:
  HC-SR501 Body Sensor Module: Pyroelectric Infrared PIR Motion Sensor Detector Module
  ESP32 - CAM: The ESP32-CAM has a very competitive small-size camera module that can operate independently as a minimum system with a footprint of only 27*40.5*4.5mm and a deep sleep current of up to 6mA.
