# Fritzing sketch trap-cam2 (saved by Fritzing 0.9.4)
circuit board: 2.4513cm x 1.51108cm

parts:
  Q2 = NPN-Transistor [package="SOT-23 [SMD]"]
  R3 = Resistor [tolerance=±5% resistance=10k package="2010 [SMD]"]
  R2 = Resistor [tolerance=±5% resistance=1k package="2010 [SMD]"]
  Enzo1 = HC-SR501 Body Sensor Module
  JP1 = Header 2 [package=springterminal-2.54mm-2]
  5v = Battery

nets:
  GND: Q2.2, Enzo1.VCC, 5v.-
  N1: Q2.0, R2.Pin_1
  N2: Q2.1, R3.Pin_0
  output: R3.Pin_1, JP1.1
  input: R2.Pin_0, Enzo1.OUT
  5V: Enzo1.GND, 5v.+

custom parts:
  HC-SR501 Body Sensor Module: Pyroelectric Infrared PIR Motion Sensor Detector Module
